# Fritzing sketch schema (saved by Fritzing 0.6.3b)
breadboards: 1

parts:
  Arduino1 = Arduino
  Q1 = Basic FET N-Channel [package="TO220 [THT]"]
  J1 = Piezo Speaker
  J2 = Infrared Proximity Sensor
  Power_plug1 = Power plug
  Componente1 = ledstrip
  Componente2 = ledstrip
  Q2 = Basic FET N-Channel [package="TO220 [THT]"]

nets:
  N1: Arduino1.D6, Q2.gate
  N2: Arduino1.D5, Q1.gate
  GND: Arduino1.GND, J2.GND, Q2.source
  VIN: Arduino1.VIN, J2.Vcc, Componente1.connector0, Componente2.connector0
  N3: Arduino1.A0, J2.Vout
  N4: Q1.drain, Componente2.connector1
  N5: J1.pin1, Power_plug1.GND
  N6: Componente1.connector1, Q2.drain
